# Fritzing sketch Projektna (saved by Fritzing 0.9.3b)
breadboards: 1

parts:
  Arduino = Arduino Uno (Rev3)
  S1 = Pushbutton [package="[THT]"]
  S2 = Pushbutton [package="[THT]"]
  S3 = Pushbutton [package="[THT]"]
  S4 = Pushbutton [package="[THT]"]
  LED1 = LED - 5mm [color="Green (570nm)" package="5 mm [THT]"]
  M1 = DC Motor
  R1 = Resistor [tolerance=±5% resistance=1k package=THT]
  R2 = Resistor [tolerance=±5% resistance=1k package=THT]
  R3 = Resistor [tolerance=±5% resistance=1k package=THT]
  R4 = Resistor [tolerance=±5% resistance=1k package=THT]
  KY-1 = Keyes Relay [package=THT]
  part = Rectifier Diode [part_number=1N4001 package="300 mil [THT]"]
  R5 = Resistor [tolerance=±5% resistance=220 package=THT]

nets:
  GND: Arduino.GND, M1.pin_2, R1.Pin_1, R2.Pin_1, R3.Pin_1, R4.Pin_1, KY-1.ground, R5.Pin_1
  N1: Arduino.D5_PWM, KY-1.signal
  N2: Arduino.D7, LED1.anode
  N3: Arduino.5V, S1.Pin_3, S1.Pin_4, S2.Pin_3, S2.Pin_4, S3.Pin_3, S3.Pin_4, S4.Pin_3, S4.Pin_4, KY-1.NO
  N4: S1.Pin_1, R1.Pin_0
  N5: S2.Pin_1, S2.Pin_2, R2.Pin_0
  N6: S3.Pin_1, S3.Pin_2, R3.Pin_0
  N7: S4.Pin_1, S4.Pin_2, R4.Pin_0
  N8: LED1.cathode, R5.Pin_0
  N9: M1.pin_1, KY-1.power, part.cathode

custom parts:
  Keyes Relay: The Keyes 5V relay module is suitable for SCM development, home appliance control. It uses a 5V~12V TIL control signal which can control DC / AC signal.
