# Fritzing sketch breadboard (saved by Fritzing 0.9.3b)
breadboards: 1

parts:
  S1 = Pushbutton [package="[THT]"]
  S2 = Pushbutton [package="[THT]"]
  S3 = Pushbutton [package="[THT]"]
  S4 = Pushbutton [package="[THT]"]
  Part1 = Arduino Uno (Rev3)
  R1 = Resistor [tolerance=±5% resistance=1k package=THT]
  R2 = Resistor [tolerance=±5% resistance=1k package=THT]
  R3 = Resistor [tolerance=±5% resistance=1k package=THT]
  R4 = Resistor [tolerance=±5% resistance=1k package=THT]
  LED1 = LED - 5mm [color="Green (555nm)" package="5 mm [THT]"]
  R5 = Resistor [tolerance=±5% resistance=220 package=THT]
  D1 = Rectifier Diode [part_number=1N4001 package="300 mil [THT]"]
  M1 = DC Motor
  KY-1 = Keyes Relay [package=THT]

nets:
  N1: S1.Pin_1, S1.Pin_2, Part1.D4, R4.Pin_1
  N2: S1.Pin_3, S1.Pin_4, S2.Pin_3, S2.Pin_4, S3.Pin_3, S3.Pin_4, S4.Pin_3, S4.Pin_4, Part1.5V, KY-1.power, KY-1.NO
  N3: S2.Pin_1, S2.Pin_2, Part1.D3_PWM, R3.Pin_1
  N4: S3.Pin_1, S3.Pin_2, Part1.D2, R2.Pin_1
  N5: S4.Pin_1, S4.Pin_2, Part1.D1/TX, R1.Pin_1
  N6: Part1.GND, R1.Pin_0, R2.Pin_0, R3.Pin_0, R4.Pin_0, R5.Pin_0, D1.cathode, M1.pin_2, KY-1.ground
  N7: Part1.D5_PWM, KY-1.signal
  N8: Part1.D7, LED1.anode
  N9: LED1.cathode, R5.Pin_1
  N10: D1.anode, M1.pin_1, KY-1.C

custom parts:
  Keyes Relay: The Keyes 5V relay module is suitable for SCM development, home appliance control. It uses a 5V~12V TIL control signal which can control DC / AC signal.
